# Fritzing sketch FlyingNemoFritz (saved by Fritzing 0.9.2b)
breadboards: 1

parts:
  Part1 = Arduino Nano (Rev3.0) (ICSP)
  Q1 = NPN-Transistor [package="TO92 [THT]"]
  IR1 = TSOP312.., 314.. [package=THT]
  LED1 = smd LED [color="Yellow (585nm)" package="0603 [SMD]"]
  R1 = Resistor [tolerance=±5% resistance=330 package=THT]
  R3 = Resistor [tolerance=±5% resistance=100 package="0603 [SMD]"]
  R4 = Resistor [tolerance=±5% resistance=22k package="0402 [SMD]"]
  C1 = Ceramic Capacitor [capacitance=100µF voltage=50V package="200 mil [THT, multilayer]"]
  BAT1 = BC9VPC [package=bc9vpc]
  LED2 = smd LED [color="Infrared (940nm)" package="0603 [SMD]"]
  RF1 = nRF8001 Bluetooth LE Breakout
  IC1 = Voltage Regulator [package=to-220-alt]
  R2 = Resistor [tolerance=±5% resistance=220 package="0402 [SMD]"]

nets:
  GND: Part1.GND, IR1.Vs, R1.Pin_1, C1.1, BAT1.V-, RF1.GND, IC1.GND, R2.Pin_0
  N1: Part1.D2, RF1.RDY
  N2: Part1.D3, Q1.B
  N3: Part1.D4, IR1.Data, R4.Pin_1
  N4: Part1.D9, RF1.RST
  N5: Part1.D10, RF1.REQ
  N6: Part1.D11/MOSI, RF1.MOSI
  N7: Part1.D12/MISO, RF1.MISO
  5V: Part1.5V, Q1.C, R3.Pin_0, RF1.VIN, IC1.OUT
  N8: Part1.D13/SCK, RF1.SCK
  N9: Q1.E, LED2.anode
  N10: IR1.GND, R3.Pin_1, R4.Pin_0, C1.0
  N11: LED1.cathode, R1.Pin_0
  N12: LED1.anode, RF1.ACT
  N13: BAT1.V+, IC1.IN
  N14: LED2.cathode, R2.Pin_1

custom parts:
  nRF8001 Bluetooth LE Breakout: nRF8001 Breakout Board
